# Fritzing sketch move_your_sleeves-Fritzing_project (saved by Fritzing 0.9.2b)
circuit board: 3.42554cm x 3.11423cm

parts:
  VCC1 = 4 x AAA Battery Mount
  M1 = DC Motor
  M2 = DC Motor
  IC1 = L293D [package=THT]
  FLORA1 = Adafruit_Flora
  R1 = Resistor [tolerance=±5% resistance=2.2k package=THT]
  R2 = Resistor [tolerance=±5% resistance=2.2k package=THT]
  R3 = Resistor [tolerance=±5% resistance=2.2k package=THT]
  R4 = Resistor [tolerance=±5% resistance=2.2k package=THT]
  R5 = Resistor [tolerance=±5% resistance=2.2k package=THT]
  Q5 = Basic FET N-Channel [package="TO220 [THT]"]
  Q3 = Basic FET N-Channel [package="TO220 [THT]"]
  Q2 = Basic FET N-Channel [package="TO220 [THT]"]
  Q4 = Basic FET N-Channel [package="TO220 [THT]"]
  Q1 = Basic FET N-Channel [package="TO220 [THT]"]
  Componente1 = LilyPad Temperature Sensor

nets:
  N1: VCC1.-, IC1.0V, FLORA1.connector7
  N2: VCC1.+, IC1.+Vmotor, IC1.+V, R1.Pin_0, R2.Pin_0, R3.Pin_0, R4.Pin_0, R5.Pin_0
  N3: M1.pin_1, IC1.Out_4_(_Controlled_by_Enable_2_)
  N4: M1.pin_2, IC1.Out_3_(_Controlled_by_Enable_2_)
  N5: M2.pin_1, IC1.Out_2_(_Controlled_by_Enable_1_)
  N6: M2.pin_2, IC1.Out_1_(_Controlled_by_Enable_1_)
  N7: IC1.Enable_1, IC1.Enable_2, R5.Pin_1, Q5.drain
  N8: IC1.In_1, R1.Pin_1, Q1.drain
  N9: IC1.In_2, R2.Pin_1, Q2.drain
  N10: IC1.In_3, R3.Pin_1, Q3.drain
  N11: IC1.In_4, R4.Pin_1, Q4.drain
  N12: FLORA1.connector1, Componente1.GND
  N13: FLORA1.connector2, Q2.source
  N14: FLORA1.connector3, Q1.source
  N15: FLORA1.connector4, Q2.gate, Q1.gate
  N16: FLORA1.connector9, Q4.source
  N17: FLORA1.connector10, Q3.source
  N18: FLORA1.connector12, Componente1.VO
  N19: FLORA1.connector13, Q5.source
  N20: FLORA1.connector14, Q5.gate, Q3.gate, Q4.gate, Componente1.VCC

custom parts:
  Basic FET N-Channel: A MOSFET N-Channel Transistor
